# Fritzing sketch Master Bluetooth (saved by Fritzing 0.9.3b)
breadboards: 1

parts:
  IR_Sensor = fc-51 [package=THT]
  UNO = Arduino Uno (Rev3)
  Bluetooth_Master = Bluetooth HC-05 Macho
  R3 = Resistor [tolerance=±5% resistance=2.2k package="2010 [SMD]"]
  R4 = Resistor [tolerance=±5% resistance=1k package="2010 [SMD]"]

nets:
  N1: IR_Sensor.pin1, UNO.D4
  GND: IR_Sensor.pin2, UNO.GND, Bluetooth_Master.GND, R3.Pin_0
  N2: IR_Sensor.pin3, UNO.5V
  N3: UNO.D0/RX, Bluetooth_Master.TXD
  N4: UNO.D1/TX, R3.Pin_1, R4.Pin_0
  VIN: UNO.VIN, Bluetooth_Master.VCC
  N5: Bluetooth_Master.RXD, R4.Pin_1
