# Fritzing sketch Slave Bluetooth (saved by Fritzing 0.9.3b)
breadboards: 1

parts:
  Bluetooth_Slave = Bluetooth HC-05 Macho
  Servo_Motor = Basic Servo
  UNO = Arduino Uno (Rev3)
  LCD_Display = LCD screen
  R3 = Resistor [tolerance=±5% resistance=2.2k package="2010 [SMD]"]
  R4 = Resistor [tolerance=±5% resistance=1k package="2010 [SMD]"]

nets:
  N1: Bluetooth_Slave.TXD, UNO.D0/RX
  N2: Bluetooth_Slave.RXD, R4.Pin_1
  VCC: Bluetooth_Slave.VCC, Servo_Motor.vcc, UNO.VIN
  GND: Bluetooth_Slave.GND, Servo_Motor.gnd, UNO.GND, LCD_Display.VSS, LCD_Display.V0, LCD_Display.R/W, LCD_Display.LED-, R3.Pin_0
  N3: Servo_Motor.pulse, UNO.D2
  N4: UNO.D8, LCD_Display.DB4
  N5: UNO.D9_PWM, LCD_Display.DB5
  N6: UNO.D10_PWM/SS, LCD_Display.DB6
  N7: UNO.D11_PWM/MOSI, LCD_Display.DB7
  N8: UNO.D1/TX, R3.Pin_1, R4.Pin_0
  N9: UNO.D6_PWM, LCD_Display.RS
  N10: UNO.D7, LCD_Display.E, LCD_Display.DB0
  5V: UNO.5V, LCD_Display.VDD, LCD_Display.LED+
